# Fritzing sketch LaziersCiruit (saved by Fritzing 0.9.1b)
breadboards: 3

parts:
  Part1 = Arduino Uno (Rev3)
  R1 = Photocell (LDR) [package=THT]
  R2 = Resistor [tolerance=±5% resistance=220 package=THT]
  Laser1 = LED - 5mm [color="Red (633nm)" package="5 mm [THT]"]
  Servo1 = Basic Servo
  R3 = Photocell (LDR) [package=THT]
  R4 = Resistor [tolerance=±5% resistance=220 package=THT]
  Laser2 = LED - 5mm [color="Red (633nm)" package="5 mm [THT]"]
  LED1 = LED - 5mm [color="Red (633nm)" package="5 mm [THT]"]
  R5 = Resistor [tolerance=±5% resistance=220 package=THT]

nets:
  N1: Part1.A0, R3.pin_0, R4.Pin_0
  N2: Part1.A1, R1.pin_0, R2.Pin_0
  N3: Part1.D13/SCK, Servo1.pulse
  N4: Part1.D2, R5.Pin_0
  5V: Part1.5V, R1.pin_1, Laser1.anode, Servo1.vcc, R3.pin_1, Laser2.anode
  GND: Part1.GND, Laser1.cathode, Servo1.gnd, Laser2.cathode, LED1.cathode
  N5: LED1.anode, R5.Pin_1

notes:
  LED Laser
